# Fritzing sketch luminch_one (saved by Fritzing 0.6.4b)
breadboards: 1

parts:
  J1 = Infrared Proximity Sensor [part_number=GP2Y0A02YK0F]
  LED1 = LED - 5mm [color="White (4500K)" current=350mA part_number=LXM3-PW61 package="5 mm [THT]"]
  Arduino1 = Arduino
  R1 = Resistor [tolerance=±5% resistance=18 package=THT]
  R2 = Resistor [tolerance=±5% resistance=220 package=THT]
  C2 = Electrolytic Capacitor [capacitance=100µF voltage=16V package="100 mil [THT, electrolytic]"]
  C1 = Electrolytic Capacitor [capacitance=100µF voltage=25V package="100 mil [THT, electrolytic]"]
  Q2 = transistor_signal_NPN_TO92_CBE [part_number=BC337]

nets:
  N1: J1.Vout, Arduino1.A0
  GND: J1.GND, Arduino1.GND, C2.-, C1.-, Q2.connector0
  VCC: J1.Vcc, LED1.anode, Arduino1.+5V, C2.+, C1.+
  N2: LED1.cathode, R1.Pin_0
  N3: Arduino1.D3, R2.Pin_1
  N4: R1.Pin_1, Q2.connector2
  N5: R2.Pin_0, Q2.connector1
